# Fritzing sketch project1 (saved by Fritzing 0.9.3b)
breadboards: 1

parts:
  Part1 = Arduino Uno (Rev3)
  J1 = Basic Servo
  J2 = Basic Servo
  S1 = SPST Switch [package=switch-spdt_lock.007s]
  S2 = SPST Switch [package=switch-spdt_lock.007s]
  U4 = LCD-16X2 [package=lcd-16x2]
  R1 = Resistor [tolerance=±5% resistance=220 package=THT]
  R2 = Resistor [tolerance=±5% resistance=220 package=THT]

nets (from the breadboard view):
  N1: Part1.D8, S1.S
  N2: Part1.D11_PWM/MOSI, U4.E
  N3: Part1.D12/MISO, U4.RS
  N4: Part1.D13/SCK, J1.pulse
  GND: Part1.GND, J1.gnd, J2.gnd, S1.O, S2.O, U4.R_W, R2.Pin_1
  N5: Part1.D2, U4.DB7
  N6: Part1.D3_PWM, U4.DB6
  N7: Part1.D4, U4.DB5
  N8: Part1.D5_PWM, U4.DB4
  N9: Part1.D7, S2.S
  VCC: Part1.5V, J1.vcc, J2.vcc, R1.Pin_1
  N10: U4.VSS, U4.VO, U4.A, R1.Pin_0
  N11: U4.VDD, U4.K, R2.Pin_0
